// Logisim project moore.circ as structural Verilog: 1 circuit, main circuit main
module main (
  input  Binary,
  input  Reset,
  output out_3
);

  wire and_1_out, and_2_out, and_3_out, and_4_out, and_5_out, and_6_out, and_7_out, and_8_out, clock_1_out,
       not_1_out, or_1_out, or_2_out, or_3_out, S0_q, S0_qn, S1_q, S1_qn, S2_q, S2_qn;

  not not_1 (not_1_out, Binary);
  and and_1 (and_1_out, S2_qn, S1_q, S0_qn, not_1_out);
  and and_2 (and_2_out, S2_q, S1_qn, S0_qn, Binary);
  and and_3 (and_3_out, S2_qn, Binary, S0_q);
  and and_4 (and_4_out, S2_qn, S1_qn, not_1_out, S0_q);
  and and_5 (and_5_out, S2_q, S1_qn, S0_qn, Binary);
  and and_6 (and_6_out, S2_qn, S1_qn, Binary);
  and and_7 (and_7_out, S2_qn, S1_q, S0_q, not_1_out);
  and and_8 (and_8_out, S2_q, S1_qn, not_1_out, S0_qn);
  or or_1 (or_1_out, and_1_out, and_2_out);
  or or_2 (or_2_out, and_3_out, and_4_out, and_5_out);
  or or_3 (or_3_out, and_6_out, and_7_out, and_8_out);
  Clock clock_1 (.out(clock_1_out));
  D_Flip_Flop S2 (.D(or_1_out), .clk(clock_1_out), .Q(S2_q), .Qn(S2_qn), .reset(Reset));  // open: preset
  D_Flip_Flop S1 (.D(or_2_out), .clk(clock_1_out), .Q(S1_q), .Qn(S1_qn), .reset(Reset));  // open: preset
  D_Flip_Flop S0 (.D(or_3_out), .clk(clock_1_out), .Q(S0_q), .Qn(S0_qn), .reset(Reset));  // open: preset
  and and_9 (out_3, S2_qn, S1_qn, S0_qn);
endmodule
